# Fritzing sketch Schematic 4 digit 7 seg (saved by Fritzing 0.9.3b)
breadboards: 1

parts:
  Part1 = Arduino Mega 2560 (Rev3)
  7_Segment1 = 7 Segment Display
  7_Segment4 = 7 Segment Display
  7_Segment5 = 7 Segment Display
  7_Segment6 = 7 Segment Display
  R1 = Resistor [tolerance=±5% resistance=220 package=THT]
  R2 = Resistor [tolerance=±5% resistance=220 package=THT]
  R3 = Resistor [tolerance=±5% resistance=220 package=THT]
  R4 = Resistor [tolerance=±5% resistance=220 package=THT]

nets:
  5V: Part1.5V
  GND: Part1.GND
  pinG: 7_Segment1.Segment_G, 7_Segment4.Segment_G, 7_Segment5.Segment_G, 7_Segment6.Segment_G
  pinF: 7_Segment1.Segment_F, 7_Segment4.Segment_F, 7_Segment5.Segment_F, 7_Segment6.Segment_F
  N1: 7_Segment1.common_anode, R4.Pin_1
  pinE: 7_Segment1.Segment_E, 7_Segment4.Segment_E, 7_Segment5.Segment_E, 7_Segment6.Segment_E
  pinD: 7_Segment1.Segment_D, 7_Segment4.Segment_D, 7_Segment5.Segment_D, 7_Segment6.Segment_D
  pin_Dp: 7_Segment1.Segment_DP, 7_Segment4.Segment_DP, 7_Segment5.Segment_DP, 7_Segment6.Segment_DP
  pinC: 7_Segment1.Segment_C, 7_Segment4.Segment_C, 7_Segment5.Segment_C, 7_Segment6.Segment_C
  pinB: 7_Segment1.Segment_B, 7_Segment4.Segment_B, 7_Segment5.Segment_B, 7_Segment6.Segment_B
  pinA: 7_Segment1.Segment_A, 7_Segment4.Segment_A, 7_Segment5.Segment_A, 7_Segment6.Segment_A
  N2: 7_Segment4.common_anode, R3.Pin_1
  N3: 7_Segment5.common_anode, R2.Pin_1
  N4: 7_Segment6.common_anode, R1.Pin_1
  D4: R1.Pin_0
  D3: R2.Pin_0
  D2: R3.Pin_0
  D1: R4.Pin_0

// code stored in the sketch: 4_digit_seven_seg.ino
#define D1 35
#define D2 37
#define D3 39
#define D4 41
#define pinA 31
#define pinB 29
#define pinC 49
#define pinD 45
#define pinE 43
#define pinF 33
#define pinG 51
#define pin_Dp 47

void setup() {
  pinMode(D1 , OUTPUT);
  pinMode(D2 , OUTPUT);
  pinMode(D3 , OUTPUT);
  pinMode(D4 , OUTPUT);
  pinMode(pinA, OUTPUT);
  pinMode(pinB, OUTPUT);
  pinMode(pinC, OUTPUT);
  pinMode(pinD, OUTPUT);
  pinMode(pinE, OUTPUT);
  pinMode(pinF, OUTPUT);
  pinMode(pinG, OUTPUT);
  pinMode(pin_Dp, OUTPUT);
}

void digit_switch(int digit){
  int switcher= digit;
  digitalWrite(D1, LOW);
  digitalWrite(D2, LOW);
  digitalWrite(D3, LOW);
  digitalWrite(D4, LOW);
  switch(switcher){
      case 1 :
        digitalWrite(D1 , HIGH);
        break;
      case 2 :
        digitalWrite(D2, HIGH);
        break;
      case 3 :
        digitalWrite(D3 , HIGH);
        break;
      case 4 :
        digitalWrite(D4 , HIGH);
        break;
    }
  }
void value(int Value){
    int value=Value;
    switch(value){
        case 0 :
        digitalWrite(pinA , LOW);
        digitalWrite(pinB , LOW);
        digitalWrite(pinC , LOW);
        digitalWrite(pinD , LOW);
        digitalWrite(pinE , LOW);
        digitalWrite(pinF , LOW);
        digitalWrite(pinG , HIGH);
        digitalWrite(pin_Dp , HIGH);
        break;

      case 1:
        digitalWrite(pinA , HIGH);
        digitalWrite(pinB , LOW);
        digitalWrite(pinC , LOW);
        digitalWrite(pinD , HIGH);
        digitalWrite(pinE , HIGH);
        digitalWrite(pinF , HIGH);
        digitalWrite(pinG , HIGH);
        digitalWrite(pin_Dp ,HIGH);
        break;
      case 2:
        digitalWrite(pinA , LOW);
        digitalWrite(pinB , LOW);
        digitalWrite(pinC , HIGH);
        digitalWrite(pinD , LOW);
        digitalWrite(pinE , LOW);
        digitalWrite(pinF , HIGH);
        digitalWrite(pinG , LOW);
        digitalWrite(pin_Dp , HIGH);
        break;
      case 3:
        digitalWrite(pinA , LOW);
        digitalWrite(pinB , LOW);
        digitalWrite(pinC , LOW);
        digitalWrite(pinD , LOW);
        digitalWrite(pinE , HIGH);
        digitalWrite(pinF , HIGH);
        digitalWrite(pinG , LOW);
        digitalWrite(pin_Dp , HIGH);
        break;
      
      case 4:
        digitalWrite(pinA , HIGH);
        digitalWrite(pinB , LOW);
        digitalWrite(pinC , LOW);
        digitalWrite(pinD , HIGH);
        digitalWrite(pinE , HIGH);
        digitalWrite(pinF , LOW);
        digitalWrite(pinG , LOW);
        digitalWrite(pin_Dp , HIGH);
        break;
      case 5:
        
        digitalWrite(pinA , LOW);
        digitalWrite(pinB , HIGH);
        digitalWrite(pinC , LOW);
        digitalWrite(pinD , LOW);
        digitalWrite(pinE , HIGH);
        digitalWrite(pinF , LOW);
        digitalWrite(pinG , LOW);
        digitalWrite(pin_Dp , HIGH);
        break;
        
      case 6:
        
        digitalWrite(pinA , LOW);
        digitalWrite(pinB , HIGH);
        digitalWrite(pinC , LOW);
        digitalWrite(pinD , LOW);
        digitalWrite(pinE , LOW);
        digitalWrite(pinF , LOW);
        digitalWrite(pinG , LOW);
        digitalWrite(pin_Dp , HIGH);
        break;
      
      case 7:
        
        digitalWrite(pinA , LOW);
        digitalWrite(pinB , LOW);
        digitalWrite(pinC , LOW);
        digitalWrite(pinD , HIGH);
        digitalWrite(pinE , HIGH);
        digitalWrite(pinF , HIGH);
        digitalWrite(pinG , HIGH);
        digitalWrite(pin_Dp , HIGH);
        break;
      case 8:
        
        digitalWrite(pinA , LOW);
        digitalWrite(pinB , LOW);
        digitalWrite(pinC , LOW);
        digitalWrite(pinD , LOW);
        digitalWrite(pinE , LOW);
        digitalWrite(pinF , LOW);
        digitalWrite(pinG , LOW);
        digitalWrite(pin_Dp , HIGH);
        break;
       
       case 9:
        digitalWrite(pinA , LOW);
        digitalWrite(pinB , LOW);
        digitalWrite(pinC , LOW);
        digitalWrite(pinD , LOW);
        digitalWrite(pinE , HIGH);
        digitalWrite(pinF , LOW);
        digitalWrite(pinG , LOW);
        digitalWrite(pin_Dp , HIGH);
        break;
   }
  }

void loop() {
digit_switch(1);
value(9);
delay(5);
digit_switch(2);
value(5);
delay(5);
digit_switch(3);
value(3);
delay(5);
digit_switch(4);
value(4);
delay(5);

 }
