# Fritzing sketch Sevent Seg Schematic diagram (saved by Fritzing 0.9.3b)
breadboards: 1

parts:
  R1 = Resistor [tolerance=±5% resistance=220 package=THT]
  R2 = Resistor [tolerance=±5% resistance=220 package=THT]
  R3 = Resistor [tolerance=±5% resistance=220 package=THT]
  R4 = Resistor [tolerance=±5% resistance=220 package=THT]
  R5 = Resistor [tolerance=±5% resistance=220 package=THT]
  R6 = Resistor [tolerance=±5% resistance=220 package=THT]
  R7 = Resistor [tolerance=±5% resistance=220 package=THT]
  R8 = Resistor [tolerance=±5% resistance=220 package=THT]
  7_Segment1 = 7 Segment Display
  Part1 = Arduino Mega 2560 (Rev3)
  V1 = DC Power [voltage=5]

nets:
  A Pin 22: R1.Pin_0, Part1.D22
  N1: R1.Pin_1, 7_Segment1.Segment_A
  B Pin 24: R2.Pin_0, Part1.D24
  N2: R2.Pin_1, 7_Segment1.Segment_B
  C Pin 26: R3.Pin_0, Part1.D26
  N3: R3.Pin_1, 7_Segment1.Segment_C
  D Pin 28: R4.Pin_0, Part1.D28
  N4: R4.Pin_1, 7_Segment1.Segment_D
  E Pin 30: R5.Pin_0, Part1.D30
  N5: R5.Pin_1, 7_Segment1.Segment_E
  F Pin 32: R6.Pin_0, Part1.D32
  N6: R6.Pin_1, 7_Segment1.Segment_F
  G Pin 34: R7.Pin_0, Part1.D34
  N7: R7.Pin_1, 7_Segment1.Segment_G
  Dp Pin 36: R8.Pin_0, Part1.D36
  N8: R8.Pin_1, 7_Segment1.Segment_DP
  GND/Ground: 7_Segment1.common_cathode, Part1.GND, V1.V-
  N9: Part1.VIN, V1.V+
