# Fritzing sketch 7 segment Counter (saved by Fritzing 0.9.3b)
breadboards: 1

parts:
  Part1 = Arduino Mega 2560 (Rev3)
  R1 = Resistor [tolerance=±5% resistance=220 package=THT]
  7_Segment1 = 7 Segment Display
  R2 = Resistor [tolerance=±5% resistance=220 package=THT]
  R3 = Resistor [tolerance=±5% resistance=220 package=THT]
  R4 = Resistor [tolerance=±5% resistance=220 package=THT]
  R5 = Resistor [tolerance=±5% resistance=220 package=THT]
  R6 = Resistor [tolerance=±5% resistance=220 package=THT]
  R7 = Resistor [tolerance=±5% resistance=220 package=THT]
  R8 = Resistor [tolerance=±5% resistance=220 package=THT]
  LED1 = LED - 5mm [color="Red (633nm)" package="5 mm [THT]"]
  R9 = Resistor [tolerance=±5% resistance=220 package=THT]

nets:
  GND: Part1.GND, 7_Segment1.common_cathode#3, LED1.cathode
  pin 13: Part1.D13_PWM, R9.Pin_0
  pin 9: Part1.D9_PWM, R8.Pin_0
  pin 8: Part1.D8_PWM, R7.Pin_0
  5V: Part1.5V
  pin 2: Part1.D2_PWM, R1.Pin_0
  pin 3: Part1.D3_PWM, R2.Pin_0
  pin 4: Part1.D4_PWM, R3.Pin_0
  pin 5: Part1.D5_PWM, R4.Pin_0
  pin 6: Part1.D6_PWM, R5.Pin_0
  pin 7: Part1.D7_PWM, R6.Pin_0
  N1: R1.Pin_1, 7_Segment1.Segment_A
  N2: 7_Segment1.Segment_F, R6.Pin_1
  N3: 7_Segment1.Segment_E, R5.Pin_1
  N4: 7_Segment1.Segment_DP, R8.Pin_1
  N5: 7_Segment1.Segment_D, R4.Pin_1
  N6: 7_Segment1.common_cathode#12, R3.Pin_1
  N7: 7_Segment1.Segment_G, R7.Pin_1
  N8: 7_Segment1.Segment_B, R2.Pin_1
  N9: LED1.anode, R9.Pin_1

notes:
  Common Cathode 7 Segment
