# Fritzing sketch IRremote_and_Receiver (saved by Fritzing 0.9.3b)
breadboards: 1

parts:
  Part1 = Arduino Mega 2560 (Rev3)
  LED1 = LED - 5mm [color="Red (633nm)" package="5 mm [THT]"]
  LED2 = LED - 5mm [color="Red (633nm)" package="5 mm [THT]"]
  LED3 = LED - 5mm [color="Red (633nm)" package="5 mm [THT]"]
  LED4 = LED - 5mm [color="Red (633nm)" package="5 mm [THT]"]
  IR1 = TSOP312.., 314.. [package=THT]
  R1 = Resistor [tolerance=±5% resistance=220 package=THT]
  R2 = Resistor [tolerance=±5% resistance=220 package=THT]
  R3 = Resistor [tolerance=±5% resistance=220 package=THT]
  R4 = Resistor [tolerance=±5% resistance=220 package=THT]

nets:
  GND/Ground: Part1.GND, LED1.cathode, LED2.cathode, LED3.cathode, LED4.cathode, IR1.GND
  Signal: Part1.D2_PWM
  Pin1: Part1.D4_PWM
  Pin2: Part1.D5_PWM
  Pin3: Part1.D6_PWM
  Pin4: Part1.D7_PWM, R1.Pin_0
  5V/VCC: Part1.5V, IR1.Vs
  N1: LED1.anode, R4.Pin_1
  N2: LED2.anode, R3.Pin_1
  N3: LED3.anode, R2.Pin_1
  N4: LED4.anode, R1.Pin_1
  Signsl: IR1.Data
  Pin5: R2.Pin_0
  Pin6: R3.Pin_0
  Pin7: R4.Pin_0
