# Fritzing sketch Security Keypad Schematic Diagram (saved by Fritzing 0.9.3b)
breadboards: 1

parts:
  Part1 = Arduino Mega 2560 (Rev3)
  LED1 = LED - 5mm [color="Red (633nm)" package="5 mm [THT]"]
  LED2 = LED - 5mm [color="Red (633nm)" package="5 mm [THT]"]
  Matrix_keypad1 = KEYPAD 4x4
  R1 = Resistor [tolerance=±5% resistance=220 package=THT]
  R2 = Resistor [tolerance=±5% resistance=220 package=THT]
  V1 = DC Power [voltage=5]

nets:
  GND/Ground: Part1.GND, LED1.cathode, LED2.cathode, V1.V-
  N1: Part1.VIN, V1.V+
  Access granted LED Pin: Part1.D2_PWM, R1.Pin_0
  Access denied LED Pin: Part1.D3_PWM, R2.Pin_0
  Row1: Part1.D22, Matrix_keypad1.row1
  Row2: Part1.D24, Matrix_keypad1.row2
  Row3: Part1.D26, Matrix_keypad1.row3
  Row4: Part1.D28, Matrix_keypad1.row4
  Col1: Part1.D30, Matrix_keypad1.col1
  Col2: Part1.D32, Matrix_keypad1.col2
  Col3: Part1.D34, Matrix_keypad1.col3
  Col4: Part1.D36, Matrix_keypad1.col4
  N2: LED1.anode, R1.Pin_1
  N3: LED2.anode, R2.Pin_1

custom parts:
  KEYPAD 4x4: Matrix keypad 16 buttons, 4 rows x 4 columns
