# Fritzing sketch LDC Display Schematic Diagram (saved by Fritzing 0.9.3b)
breadboards: 1

parts:
  LCD1 = LCD screen
  Part1 = Arduino Mega 2560 (Rev3)
  R1 = Trimmer Potentiometer [maximum_resistance=10kΩ package=THT]
  R2 = Trimmer Potentiometer [maximum_resistance=10kΩ package=THT]
  V1 = DC Power [voltage=5]

nets:
  GND/Ground: LCD1.VSS, LCD1.R/W, LCD1.LED-, Part1.GND, R1.leg1, R2.leg1, V1.V-
  V Supply: LCD1.VDD, R1.leg2, R2.leg2
  N1: LCD1.V0, R1.wiper
  RS Pin: LCD1.RS, Part1.D32
  EN Pin: LCD1.E, Part1.D30
  DB 4 Pin: LCD1.DB4, Part1.D28
  DB 5 Pin: LCD1.DB5, Part1.D26
  DB 6 Pin: LCD1.DB6, Part1.D24
  DB 7 Pin: LCD1.DB7, Part1.D22
  N2: LCD1.LED+, R2.wiper
  N3: Part1.VIN, V1.V+
