# Fritzing sketch Nokia_5110_LCD Schematic Diagram (saved by Fritzing 0.9.3b)
breadboards: 1

parts:
  Nokia_5110_LCD_Module1 = Nokia 5110 LCD
  Part1 = Arduino Mega 2560 (Rev3)
  S1 = Pushbutton [package="[THT]"]
  S2 = Pushbutton [package="[THT]"]
  S3 = Pushbutton [package="[THT]"]
  R1 = Resistor [tolerance=±5% resistance=220 package=THT]
  R2 = Resistor [tolerance=±5% resistance=220 package=THT]
  R3 = Resistor [tolerance=±5% resistance=220 package=THT]
  V1 = DC Power [voltage=5]
  R4 = Resistor [tolerance=±5% resistance=220 package=THT]
  R5 = Resistor [tolerance=±5% resistance=220 package=THT]
  R6 = Resistor [tolerance=±5% resistance=220 package=THT]
  R7 = Resistor [tolerance=±5% resistance=220 package=THT]
  R8 = Resistor [tolerance=±5% resistance=220 package=THT]
  R9 = Resistor [tolerance=±5% resistance=220 package=THT]

nets:
  5V Supply/LED Pin: Nokia_5110_LCD_Module1.VCC, Part1.5V, S1.Pin_3, S1.Pin_4, S2.Pin_3, S2.Pin_4, S3.Pin_3, S3.Pin_4, R1.Pin_1, R2.Pin_1, R3.Pin_1, R9.Pin_0
  GND/Ground: Nokia_5110_LCD_Module1.GND, Part1.GND, R1.Pin_0, R2.Pin_0, R3.Pin_0, V1.V-
  N1: Nokia_5110_LCD_Module1.SCE, Nokia_5110_LCD_Module1.SCE_(out), R5.Pin_1
  N2: Nokia_5110_LCD_Module1.RST, R6.Pin_1
  N3: Nokia_5110_LCD_Module1.D/C, R7.Pin_1
  N4: Nokia_5110_LCD_Module1.DN(MOSI), R8.Pin_1
  N5: Nokia_5110_LCD_Module1.SCLK, R4.Pin_1
  N6: Nokia_5110_LCD_Module1.LED, R9.Pin_1
  N7: Part1.VIN, V1.V+
  CLK Pin: Part1.D2_PWM, R4.Pin_0
  DN Pin: Part1.D3_PWM, R8.Pin_0
  D/C Pin: Part1.D4_PWM, R7.Pin_0
  SCE Pin: Part1.D5_PWM, R5.Pin_0
  RST Pin: Part1.D6_PWM, R6.Pin_0
  Down Button Pin: Part1.D22, S2.Pin_1
  Enter Button Pin: Part1.D24, S3.Pin_1
  Up Button Pin: Part1.D26, S1.Pin_1, S1.Pin_2

custom parts:
  Nokia 5110 LCD: Nokia 5110 Graphic 84*48 LCD module such as the Sparkfun LCD-10168 or the clones from Ebay. There is example code for the Arduino available from the Sparkfun site in https://learn.sparkfun.com/tutorials/graphic-lcd-hookup-guide This is a 3.3V device, if you are running it from a 5V micro you need a 5V tolorant level translator such as the 74ahc367 to protect the signal imputs. Rafa G. did a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
