# Fritzing sketch Schematic (saved by Fritzing 0.9.3b)
breadboards: 1

parts:
  Part1 = Arduino Uno (Rev3)
  R1 = Resistor [tolerance=±5% resistance=220 package=THT]
  S1 = Pushbutton [package="[THT]"]

nets:
  pin_8: Part1.D8, S1.Pin_1, S1.Pin_2
  N1: Part1.GND, R1.Pin_0
  N2: Part1.5V, R1.Pin_1, S1.Pin_3, S1.Pin_4
