# Fritzing sketch Schematic (saved by Fritzing 0.9.3b)
breadboards: 1

parts:
  Part1 = Arduino Mega 2560 (Rev3)
  R1 = Resistor [tolerance=±5% resistance=220 package=THT]
  R2 = Resistor [tolerance=±5% resistance=220 package=THT]
  R3 = Resistor [tolerance=±5% resistance=220 package=THT]
  R4 = Resistor [tolerance=±5% resistance=220 package=THT]
  R5 = Resistor [tolerance=±5% resistance=220 package=THT]
  R6 = Resistor [tolerance=±5% resistance=220 package=THT]
  R7 = Resistor [tolerance=±5% resistance=220 package=THT]
  R8 = Resistor [tolerance=±5% resistance=220 package=THT]
  R9 = Resistor [tolerance=±5% resistance=220 package=THT]
  R10 = Resistor [tolerance=±5% resistance=220 package=THT]
  R11 = Resistor [tolerance=±5% resistance=220 package=THT]
  R12 = Resistor [tolerance=±5% resistance=220 package=THT]
  R13 = Resistor [tolerance=±5% resistance=220 package=THT]
  R14 = Resistor [tolerance=±5% resistance=220 package=THT]
  R15 = Resistor [tolerance=±5% resistance=220 package=THT]
  R16 = Resistor [tolerance=±5% resistance=220 package=THT]
  S1 = Pushbutton [package="[THT]"]
  S2 = Pushbutton [package="[THT]"]
  R17 = Resistor [tolerance=±5% resistance=220 package=THT]
  R18 = Resistor [tolerance=±5% resistance=220 package=THT]
  R19 = Trimmer Potentiometer [maximum_resistance=10kΩ package=THT]
  7_Segment2 = 7 Segment Display
  7_Segment3 = 7 Segment Display
  7_Segment4 = 7 Segment Display

nets:
  GND: Part1.GND, R17.Pin_0, R18.Pin_0, R19.leg2
  5V/Vcc: Part1.5V, S1.Pin_3, S1.Pin_4, S2.Pin_3, S2.Pin_4, R17.Pin_1, R18.Pin_1, R19.leg1
  N1: R1.Pin_1, 7_Segment2.Segment_A#10, 7_Segment3.Segment_A#10
  N2: R2.Pin_1, 7_Segment2.Segment_B, 7_Segment3.Segment_B
  N3: R3.Pin_1, 7_Segment2.Segment_C, 7_Segment3.Segment_C
  N4: R4.Pin_1, 7_Segment2.Segment_D, 7_Segment3.Segment_D
  N5: R5.Pin_1, 7_Segment2.Segment_E, 7_Segment3.Segment_E
  N6: R6.Pin_1, 7_Segment2.Segment_F, 7_Segment3.Segment_F
  N7: R7.Pin_1, 7_Segment2.Segment_A#1, 7_Segment3.Segment_A#1
  N8: R8.Pin_1, 7_Segment2.Segment_DP, 7_Segment3.Segment_DP
  N9: R9.Pin_1, 7_Segment4.Segment_A#10
  N10: R10.Pin_1, 7_Segment4.Segment_B
  N11: R11.Pin_1, 7_Segment4.Segment_C
  N12: R12.Pin_1, 7_Segment4.Segment_D
  N13: R13.Pin_1, 7_Segment4.Segment_E
  N14: R14.Pin_1, 7_Segment4.Segment_F
  N15: R15.Pin_1, 7_Segment4.Segment_A#1
  N16: R16.Pin_1, 7_Segment4.Segment_DP
