# Fritzing sketch Schematic (saved by Fritzing 0.9.3b)
breadboards: 1

parts:
  Part1 = Arduino Uno (Rev3)
  J1 = Basic Servo

nets:
  Yellow/Orange wire: Part1.D9_PWM, J1.pulse
  Red Wire: Part1.5V, J1.vcc
  Black/Brown wire: Part1.GND, J1.gnd
