# Fritzing sketch Sonic Sensor Schematic (saved by Fritzing 0.9.3b)
breadboards: 1

parts:
  Part1 = Arduino Mega 2560 (Rev3)
  U1 = LCD-16X2 [package=lcd-16x2]
  R1 = Trimmer Potentiometer [maximum_resistance=10kΩ package=THT]
  hc-sr1 = hc-sr04
  R2 = Resistor [tolerance=±5% resistance=220 package=THT]
  R3 = Resistor [tolerance=±5% resistance=220 package=THT]
  R4 = Resistor [tolerance=±5% resistance=220 package=THT]
  LED1 = smd LED [color="Red (633nm)" package="0805 [SMD]"]
  LED2 = smd LED [color="Green (560nm)" package="0805 [SMD]"]

nets:
  pin 2: Part1.D2_PWM, R3.Pin_0
  pin 3: Part1.D3_PWM, R4.Pin_0
  GND/pin 22/pin 23: Part1.D22, Part1.D23, U1.R_W, U1.K, R1.wiper, hc-sr1.Trig, LED1.cathode, LED2.cathode
  pin 28: Part1.D28, U1.DB7
  pin 30: Part1.D30, U1.DB6
  pin 31: Part1.D31, U1.E
  pin 32: Part1.D32, U1.DB5
  pin 33: Part1.D33, U1.RS
  pin 34: Part1.D34, U1.DB4
  pin 40: Part1.D40
  pin 41: Part1.D41
  N1: U1.VO, R1.leg2
  N2: U1.A, R2.Pin_1
  5V/VCC: R1.leg1, hc-sr1.VCC, R2.Pin_0
  N3: R3.Pin_1, LED1.anode
  N4: R4.Pin_1, LED2.anode
