# Fritzing sketch step motor (saved by Fritzing 0.9.3b)
breadboards: 1

parts:
  Part1 = Arduino Mega 2560 (Rev3)
  IC1 = L293D [package=THT]
  R1 = Resistor [tolerance=±5% resistance=220 package=THT]
  R2 = Resistor [tolerance=±5% resistance=220 package=THT]
  R3 = Resistor [tolerance=±5% resistance=220 package=THT]
  R4 = Resistor [tolerance=±5% resistance=220 package=THT]
  LED1 = LEDs [package=led10mm]
  LED2 = LEDs [package=led10mm]
  LED3 = LEDs [package=led10mm]
  LED4 = LEDs [package=led10mm]
  M1 = Stepper Motor - Bipolar

nets:
  5V: Part1.5V, IC1.+V
  net label: Part1.D2_PWM, Part1.D3_PWM, Part1.D4_PWM, Part1.D5_PWM, IC1.Enable_1, IC1.In_1, IC1.In_2, IC1.+Vmotor, IC1.Enable_2, IC1.In_3, IC1.In_4
  GND: Part1.GND, IC1.0V
  N1: IC1.Out_1_(_Controlled_by_Enable_1_), R1.Pin_0
  N2: IC1.Out_2_(_Controlled_by_Enable_1_), R2.Pin_0
  N3: IC1.Out_3_(_Controlled_by_Enable_2_), R3.Pin_0
  N4: IC1.Out_4_(_Controlled_by_Enable_2_), R4.Pin_0
  N5: R1.Pin_1, LED1.A
  N6: R2.Pin_1, LED2.A
  N7: R3.Pin_1, LED3.A
  N8: R4.Pin_1, LED4.A
  N9: LED1.C, M1.A
  N10: LED2.C, M1.B
  N11: LED3.C, M1.C
  N12: LED4.C, M1.D
