# Fritzing sketch Schematic (saved by Fritzing 0.9.3b)
breadboards: 1

parts:
  Part1 = Arduino Uno (Rev3)
  R1 = Resistor [tolerance=±5% resistance=220 package=THT]
  R2 = Resistor [tolerance=±5% resistance=220 package=THT]
  R3 = Resistor [tolerance=±5% resistance=220 package=THT]
  R4 = Resistor [tolerance=±5% resistance=220 package=THT]
  LED1 = LED - 5mm [color="White (4500K)" package="5 mm [THT]"]
  LED3 = LED - 5mm [color="Orange (620nm)" package="5 mm [THT]"]
  LED4 = LED - 5mm [color="Blue (525nm)" package="5 mm [THT]"]
  Part2 = Thumb Joystick
  LED2 = smd LED [color="Green (570nm)" package="0603 [SMD]"]

nets:
  pin_A0: Part1.A0, Part2.HORZ
  pin_A1: Part1.A1, Part2.VERT
  N1: Part1.D8, R1.Pin_0
  N2: Part1.D9_PWM, R2.Pin_0
  N3: Part1.D10_PWM/SS, R3.Pin_0
  N4: Part1.D11_PWM/MOSI, R4.Pin_0
  N5: Part1.D7, Part2.SEL
  5V: Part1.5V, Part2.VCC
  GND: Part1.GND, LED1.cathode, LED3.cathode, LED4.cathode, Part2.GND, LED2.cathode
  N6: R1.Pin_1, LED4.anode
  N7: R2.Pin_1, LED3.anode
  N8: R3.Pin_1, LED2.anode
  N9: R4.Pin_1, LED1.anode
